# Fritzing sketch BNB (saved by Fritzing 0.9.2b)
circuit board: 3.47649cm x 2.21689cm
breadboards: 1

parts:
  Part1 = Arduino Uno (Rev3) - ICSP
  VIN_ESP = female pin header, 1 pin [form="♀ (female)"]
  GND_ESP = female pin header, 1 pin [form="♀ (female)"]
  RXD_ESP = female pin header, 1 pin [form="♀ (female)"]
  TXD_ESP = female pin header, 1 pin [form="♀ (female)"]
  ESP_RST = female pin header, 1 pin [form="♀ (female)"]
  D0_RFID = female pin header, 1 pin [form="♀ (female)"]
  D1_RFID = female pin header, 1 pin [form="♀ (female)"]
  BEEP_RFID = female pin header, 1 pin [form="♀ (female)"]
  GND_RFID = female pin header, 1 pin [form="♀ (female)"]
  VIN_RFID = female pin header, 1 pin [form="♀ (female)"]
  SDA_LCD = female pin header, 1 pin [form="♀ (female)"]
  SCL_LCD = female pin header, 1 pin [form="♀ (female)"]
  VIN_LCD = female pin header, 1 pin [form="♀ (female)"]
  GND_LCD = female pin header, 1 pin [form="♀ (female)"]
  12_IN = female pin header, 1 pin [form="♀ (female)"]
  12_IN_GND = female pin header, 1 pin [form="♀ (female)"]
  5v_GND = female pin header, 1 pin [form="♀ (female)"]
  5v_OUT = female pin header, 1 pin [form="♀ (female)"]
  12_SRC = female pin header, 1 pin [form="♀ (female)"]
  12v_SRC_GND = female pin header, 1 pin [form="♀ (female)"]
  R1 = Resistor [tolerance=±5% resistance=10k package=THT]
  R2 = Resistor [tolerance=±5% resistance=20k package=THT]
  BTN_GND = female pin header, 1 pin [form="♀ (female)"]
  BTN_IN = female pin header, 1 pin [form="♀ (female)"]
  GND_LED = female pin header, 1 pin [form="♀ (female)"]
  RED_LED = female pin header, 1 pin [form="♀ (female)"]
  GREEN_LED = female pin header, 1 pin [form="♀ (female)"]
  BLUE_LED = female pin header, 1 pin [form="♀ (female)"]
  R3 = Resistor [tolerance=±5% resistance=2.2k package=THT]
  R4 = Resistor [tolerance=±5% resistance=330 package=THT]
  R5 = Resistor [tolerance=±5% resistance=330 package=THT]
  R6 = Resistor [tolerance=±5% resistance=330 package=THT]
  GND_UNO = female pin header, 1 pin [form="♀ (female)"]
  UNO_VIN = female pin header, 1 pin [form="♀ (female)"]
  UNO_12 = female pin header, 1 pin [form="♀ (female)"]
  UNO_11 = female pin header, 1 pin [form="♀ (female)"]
  UNO_10 = female pin header, 1 pin [form="♀ (female)"]
  UNO_9 = female pin header, 1 pin [form="♀ (female)"]
  UNO_6 = female pin header, 1 pin [form="♀ (female)"]

nets:
  N1: Part1.A4/SDA, SDA_LCD.pin1
  N2: Part1.A5/SCL, SCL_LCD.pin1
  N3: Part1.ICSP_MISO, Part1.D12/MISO, R1.Pin_1, R2.Pin_0, UNO_12.pin1
  N4: Part1.GND, GND_ESP.pin1, GND_RFID.pin1, GND_LCD.pin1, 12_IN_GND.pin1, 5v_GND.pin1, 12v_SRC_GND.pin1, R2.Pin_1, GND_LED.pin1, R3.Pin_1, GND_UNO.pin1
  N5: Part1.D8, RXD_ESP.pin1
  N6: Part1.D9_PWM, R4.Pin_1, UNO_9.pin1
  N7: Part1.D10_PWM/SS, R5.Pin_1, UNO_10.pin1
  N8: Part1.D11_PWM/MOSI, R6.Pin_1, UNO_11.pin1
  N9: Part1.D2, D0_RFID.pin1
  N10: Part1.D3_PWM, D1_RFID.pin1
  N11: Part1.D4, BEEP_RFID.pin1
  N12: Part1.D6_PWM, BTN_GND.pin1, R3.Pin_0, UNO_6.pin1
  N13: Part1.D7, TXD_ESP.pin1
  N14: Part1.VIN, VIN_ESP.pin1, VIN_LCD.pin1, 5v_OUT.pin1, BTN_IN.pin1, UNO_VIN.pin1
  N15: ESP_RST.pin1, R1.Pin_0
  N16: VIN_RFID.pin1, 12_IN.pin1, 12_SRC.pin1
  N17: RED_LED.pin1, R4.Pin_0
  N18: GREEN_LED.pin1, R5.Pin_0
  N19: BLUE_LED.pin1, R6.Pin_0

notes:
  12v to 5v
  BNBT
